// Logisim project ULA.circ as structural Verilog: 20 circuits, main circuit Subtrator Maior/Menor
module Subtrator_Maior_Menor (
  input  A3,
  input  A2,
  input  A1,
  input  A0,
  input  B3,
  input  B2,
  input  B1,
  input  B0,
  output out_9,
  output out_10,
  output out_11,
  output out_12
);

  wire subtratorc1_1_t_out, subtratorc1_2_t_out, subtratorc1_3_t_out, subtratorh_1_t_out;

  SubtratorH subtratorh_1 (.A(A0), .B(B0), .S(out_9), .T_out(subtratorh_1_t_out));
  SubtratorC1 subtratorc1_1 (.A(A1), .B(B1), .T_in(subtratorh_1_t_out), .S(out_10), .T_out(subtratorc1_1_t_out));
  SubtratorC1 subtratorc1_2 (.A(A2), .B(B2), .T_in(subtratorc1_1_t_out), .S(out_11), .T_out(subtratorc1_2_t_out));
  SubtratorC1 subtratorc1_3 (.A(A3), .B(B3), .T_in(subtratorc1_2_t_out), .S(out_12), .T_out(subtratorc1_3_t_out));
endmodule

module SubtratorC1 (
  input  A,
  input  B,
  input  T_in,
  output S,
  output T_out
);

  wire and_1_out, and_2_out, and_3_out, not_1_out, not_2_out, xor_1_out;

  xor xor_1 (xor_1_out, A, B);
  not not_1 (not_1_out, A);
  not not_2 (not_2_out, A);
  and and_1 (and_1_out, B, T_in);
  and and_2 (and_2_out, T_in, not_1_out);
  and and_3 (and_3_out, B, not_2_out);
  xor xor_2 (S, xor_1_out, T_in);
  or or_1 (T_out, and_1_out, and_2_out, and_3_out);
endmodule

module SubtratorH (
  input  A,
  input  B,
  output S,
  output T_out
);

  wire not_1_out;

  not not_1 (not_1_out, A);
  xor xor_1 (S, A, B);
  and and_1 (T_out, B, not_1_out);
endmodule

module Comparador (
  input  a0,
  input  a1,
  input  a2,
  input  a3,
  input  b0,
  input  b1,
  input  b2,
  input  b3,
  output AeqB,
  output AltB_A_B,
  output AgtB_A_B
);

  wire and_1_out, and_2_out, and_3_out, and_4_out, not_1_out, not_2_out, not_3_out, not_4_out, xnor_1_out,
       xnor_2_out, xnor_3_out, xnor_4_out;

  xnor xnor_1 (xnor_1_out, a3, b3);
  xnor xnor_2 (xnor_2_out, a2, b2);
  xnor xnor_3 (xnor_3_out, a1, b1);
  xnor xnor_4 (xnor_4_out, a0, b0);
  not not_1 (not_1_out, b3);
  not not_2 (not_2_out, b2);
  not not_3 (not_3_out, b1);
  not not_4 (not_4_out, b0);
  and and_1 (and_1_out, not_1_out, a3);
  and and_2 (and_2_out, xnor_1_out, not_2_out, a2);
  and and_3 (and_3_out, xnor_1_out, xnor_2_out, not_3_out, a1);
  and and_4 (and_4_out, xnor_1_out, xnor_2_out, xnor_3_out, not_4_out, a0);
  and and_5 (AeqB, xnor_1_out, xnor_2_out, xnor_3_out, xnor_4_out);
  or or_1 (AgtB_A_B, and_1_out, and_2_out, and_3_out, and_4_out);
  nor nor_1 (AltB_A_B, AeqB, AgtB_A_B);

  // Notes on the sheet:
  //   a3
  //   b3
  //   a2
  //   b2
  //   a1
  //   b1
  //   a0
  //   b0
endmodule

module SomadorH (
  input  A,
  input  B,
  output S,
  output C_out
);

  xor xor_1 (S, A, B);
  and and_1 (C_out, B, A);
endmodule

module SomadorF1 (
  input  A,
  input  B,
  input  Cin,
  output S,
  output C_out
);

  wire and_1_out, and_2_out, and_3_out, xor_1_out;

  xor xor_1 (xor_1_out, A, B);
  and and_1 (and_1_out, B, Cin);
  and and_2 (and_2_out, Cin, A);
  and and_3 (and_3_out, B, A);
  xor xor_2 (S, xor_1_out, Cin);
  or or_1 (C_out, and_1_out, and_2_out, and_3_out);
endmodule

module Somador (
  input  in_1,
  input  in_2,
  input  in_3,
  input  in_4,
  input  in_5,
  input  in_6,
  input  in_7,
  input  in_8,
  output out_9,
  output out_10,
  output out_11,
  output out_12
);

  wire somadorf1_1_c_out, somadorf1_2_c_out, somadorf1_3_c_out, somadorh_1_c_out;

  SomadorH somadorh_1 (.A(in_1), .B(in_5), .S(out_9), .C_out(somadorh_1_c_out));
  SomadorF1 somadorf1_1 (.A(in_2), .B(in_6), .Cin(somadorh_1_c_out), .S(out_10), .C_out(somadorf1_1_c_out));
  SomadorF1 somadorf1_2 (.A(in_3), .B(in_7), .Cin(somadorf1_1_c_out), .S(out_11), .C_out(somadorf1_2_c_out));
  SomadorF1 somadorf1_3 (.A(in_4), .B(in_8), .Cin(somadorf1_2_c_out), .S(out_12), .C_out(somadorf1_3_c_out));
  // also tied to GND on the sheet: somadorf1_3_c_out
endmodule

module Multiplicador (
  input  in_1,
  input  A,
  input  in_3,
  input  in_4,
  input  in_5,
  input  B,
  input  in_7,
  input  in_8,
  output c0,
  output c1,
  output c2,
  output c3
);

  wire and_1_out, and_2_out, and_3_out, and_4_out, and_5_out, and_6_out, and_7_out, and_8_out, and_9_out,
       somadorf1_1_c_out, somadorf1_1_s, somadorf1_2_c_out, somadorf1_2_s, somadorf1_3_c_out,
       somadorf1_4_c_out, somadorf1_4_s, somadorh_1_c_out;

  and and_1 (and_1_out, in_5, A);
  and and_2 (and_2_out, B, in_1);
  and and_3 (and_3_out, in_5, in_3);
  and and_4 (and_4_out, A, B);
  and and_5 (and_5_out, in_7, in_1);
  and and_6 (and_6_out, in_5, in_4);
  and and_7 (and_7_out, B, in_3);
  and and_8 (and_8_out, in_7, A);
  and and_9 (and_9_out, in_1, in_8);
  SomadorF1 somadorf1_1 (
    .A(and_3_out), .B(and_4_out), .Cin(somadorh_1_c_out), .S(somadorf1_1_s), .C_out(somadorf1_1_c_out));
  SomadorF1 somadorf1_2 (
    .A(and_6_out), .B(and_7_out), .Cin(somadorf1_3_c_out), .S(somadorf1_2_s), .C_out(somadorf1_2_c_out));
  and and_10 (c0, in_1, in_5);
  SomadorH somadorh_1 (.A(and_1_out), .B(and_2_out), .S(c1), .C_out(somadorh_1_c_out));
  SomadorF1 somadorf1_3 (.A(somadorf1_1_s), .B(and_5_out), .Cin(somadorf1_1_c_out), .S(c2), .C_out(somadorf1_3_c_out));
  SomadorF1 somadorf1_4 (
    .A(and_8_out), .B(somadorf1_2_s), .Cin(somadorf1_2_c_out), .S(somadorf1_4_s), .C_out(somadorf1_4_c_out));
  SomadorF1 somadorf1_5 (.A(and_9_out), .B(somadorf1_4_s), .Cin(somadorf1_4_c_out), .S(c3));  // open: C_out
endmodule

module Multiplexador (
  input  in_1,
  input  in_2,
  input  in_3,
  input  in_4,
  input  C1,
  input  C2,
  output S
);

  wire and_1_out, and_2_out, and_3_out, and_4_out, not_1_out, not_2_out, not_3_out, not_4_out;

  not not_1 (not_1_out, C1);
  not not_2 (not_2_out, C2);
  not not_3 (not_3_out, C1);
  not not_4 (not_4_out, C2);
  and and_1 (and_1_out, in_1, not_1_out, not_2_out);
  and and_2 (and_2_out, in_2, not_3_out, C2);
  and and_3 (and_3_out, in_3, not_4_out, C1);
  and and_4 (and_4_out, in_4, C1, C2);
  or or_1 (S, and_1_out, and_2_out, and_3_out, and_4_out);
endmodule

module Subtrator_Menor_Maior (
  input  in_1,
  input  in_2,
  input  in_3,
  input  in_4,
  input  in_5,
  input  in_6,
  input  in_7,
  input  in_8,
  output out_9,
  output out_10,
  output out_11,
  output out_12
);

  wire not_1_out, not_2_out, not_3_out, not_4_out, somadorh_1_c_out, somadorh_2_c_out, somadorh_3_c_out,
       somadorh_4_c_out, subtratorc1_1_s, subtratorc1_1_t_out, subtratorc1_2_s, subtratorc1_2_t_out,
       subtratorc1_3_s, subtratorc1_3_t_out, subtratorh_1_s, subtratorh_1_t_out;

  SubtratorH subtratorh_1 (.A(in_5), .B(in_1), .S(subtratorh_1_s), .T_out(subtratorh_1_t_out));
  SubtratorC1 subtratorc1_1 (
    .A(in_6), .B(in_2), .T_in(subtratorh_1_t_out), .S(subtratorc1_1_s), .T_out(subtratorc1_1_t_out));
  SubtratorC1 subtratorc1_2 (
    .A(in_7), .B(in_3), .T_in(subtratorc1_1_t_out), .S(subtratorc1_2_s), .T_out(subtratorc1_2_t_out));
  SubtratorC1 subtratorc1_3 (
    .A(in_8), .B(in_4), .T_in(subtratorc1_2_t_out), .S(subtratorc1_3_s), .T_out(subtratorc1_3_t_out));
  not not_1 (not_1_out, subtratorh_1_s);
  not not_2 (not_2_out, subtratorc1_1_s);
  not not_3 (not_3_out, subtratorc1_2_s);
  not not_4 (not_4_out, subtratorc1_3_s);
  SomadorH somadorh_1 (.A(1'b1), .B(not_1_out), .S(out_12), .C_out(somadorh_1_c_out));
  SomadorH somadorh_2 (.A(somadorh_1_c_out), .B(not_2_out), .S(out_11), .C_out(somadorh_2_c_out));
  SomadorH somadorh_3 (.A(somadorh_2_c_out), .B(not_3_out), .S(out_10), .C_out(somadorh_3_c_out));
  SomadorH somadorh_4 (.A(somadorh_3_c_out), .B(not_4_out), .S(out_9), .C_out(somadorh_4_c_out));
endmodule

module Subtrator_Mestre (
  input  in_1,
  input  A,
  input  in_3,
  input  in_4,
  input  in_5,
  input  B,
  input  in_7,
  input  in_8,
  output out_9,
  output out_10,
  output out_11,
  output out_12
);

  wire comparador_1_altb_a_b, not_1_out, subtrator_maior_menor_1_out_9, subtrator_maior_menor_1_out_10,
       subtrator_maior_menor_1_out_11, subtrator_maior_menor_1_out_12, subtrator_menor_maior_1_out_9,
       subtrator_menor_maior_1_out_10, subtrator_menor_maior_1_out_11, subtrator_menor_maior_1_out_12;

  Comparador comparador_1 (
    .a0(in_1), .a1(A), .a2(in_3), .a3(in_4), .b0(in_5), .b1(B), .b2(in_7), .b3(in_8),
    .AltB_A_B(comparador_1_altb_a_b));  // open: AeqB, AgtB_A_B
  not not_1 (not_1_out, comparador_1_altb_a_b);
  Subtrator_Maior_Menor subtrator_maior_menor_1 (
    .A3(in_4), .A2(in_3), .A1(A), .A0(in_1), .B3(in_8), .B2(in_7), .B1(B), .B0(in_5),
    .out_9(subtrator_maior_menor_1_out_9), .out_10(subtrator_maior_menor_1_out_10),
    .out_11(subtrator_maior_menor_1_out_11), .out_12(subtrator_maior_menor_1_out_12));
  Subtrator_Menor_Maior subtrator_menor_maior_1 (
    .in_1(in_5), .in_2(B), .in_3(in_7), .in_4(in_8), .in_5(in_1), .in_6(A), .in_7(in_3), .in_8(in_4),
    .out_9(subtrator_menor_maior_1_out_9), .out_10(subtrator_menor_maior_1_out_10),
    .out_11(subtrator_menor_maior_1_out_11), .out_12(subtrator_menor_maior_1_out_12));
  SubMestreCon submestrecon_1 (
    .in_1(subtrator_maior_menor_1_out_9), .in_2(subtrator_maior_menor_1_out_10),
    .in_3(subtrator_maior_menor_1_out_11), .in_4(subtrator_maior_menor_1_out_12),
    .in_5(subtrator_menor_maior_1_out_12), .in_6(subtrator_menor_maior_1_out_11),
    .in_7(subtrator_menor_maior_1_out_10), .in_8(subtrator_menor_maior_1_out_9), .in_9(not_1_out),
    .out_10(out_9), .out_11(out_10), .out_12(out_11), .out_13(out_12));
endmodule

module SubMestreCon (
  input  in_1,
  input  in_2,
  input  in_3,
  input  in_4,
  input  in_5,
  input  in_6,
  input  in_7,
  input  in_8,
  input  in_9,
  output out_10,
  output out_11,
  output out_12,
  output out_13
);

  wire and_1_out, and_2_out, and_3_out, and_4_out, and_5_out, and_6_out, and_7_out, and_8_out, not_1_out,
       not_2_out, not_3_out, not_4_out;

  and and_1 (and_1_out, in_1, in_9);
  and and_2 (and_2_out, in_2, in_9);
  and and_3 (and_3_out, in_3, in_9);
  and and_4 (and_4_out, in_4, in_9);
  and and_5 (and_5_out, in_5, not_1_out);
  not not_1 (not_1_out, in_9);
  and and_6 (and_6_out, in_6, not_2_out);
  not not_2 (not_2_out, in_9);
  and and_7 (and_7_out, in_7, not_3_out);
  not not_3 (not_3_out, in_9);
  and and_8 (and_8_out, in_8, not_4_out);
  not not_4 (not_4_out, in_9);
  or or_1 (out_10, and_1_out, and_5_out);
  or or_2 (out_11, and_2_out, and_6_out);
  or or_3 (out_12, and_3_out, and_7_out);
  or or_4 (out_13, and_4_out, and_8_out);
endmodule

module Multiplexador_4 (
  input  in_1,
  input  in_2,
  input  in_3,
  input  in_4,
  input  in_5,
  input  in_6,
  input  in_7,
  input  in_8,
  input  in_9,
  input  in_10,
  input  in_11,
  input  in_12,
  input  in_13,
  input  in_14,
  input  in_15,
  input  in_16,
  input  in_17,
  input  in_18,
  output out_19,
  output out_20,
  output out_21,
  output out_22
);

  Multiplexador multiplexador_1 (
    .in_1(in_1), .in_2(in_2), .in_3(in_3), .in_4(in_4), .C1(in_17), .C2(in_18), .S(out_19));
  Multiplexador multiplexador_2 (
    .in_1(in_5), .in_2(in_6), .in_3(in_7), .in_4(in_8), .C1(in_17), .C2(in_18), .S(out_20));
  Multiplexador multiplexador_3 (
    .in_1(in_9), .in_2(in_10), .in_3(in_11), .in_4(in_12), .C1(in_17), .C2(in_18), .S(out_21));
  Multiplexador multiplexador_4 (
    .in_1(in_13), .in_2(in_14), .in_3(in_15), .in_4(in_16), .C1(in_17), .C2(in_18), .S(out_22));
endmodule

module ULA (
  input  in_1,
  input  in_2,
  input  in_3,
  input  in_4,
  input  in_5,
  input  in_6,
  input  in_7,
  input  in_8,
  input  in_9,
  input  _0___Soma,
  output out_11,
  output out_12,
  output out_13,
  output out_14
);

  wire and_1_out, Comparador_aeqb, Comparador_agtb_a_b, Comparador_altb_a_b, Multiplicador_c0,
       Multiplicador_c1, Multiplicador_c2, Multiplicador_c3, not_1_out, Somador_out_9, Somador_out_10,
       Somador_out_11, Somador_out_12, Subtrator_out_9, Subtrator_out_10, Subtrator_out_11, Subtrator_out_12;

  Somador Somador (
    .in_1(in_1), .in_2(in_2), .in_3(in_3), .in_4(in_4), .in_5(in_5), .in_6(in_6), .in_7(in_7), .in_8(in_8),
    .out_9(Somador_out_9), .out_10(Somador_out_10), .out_11(Somador_out_11), .out_12(Somador_out_12));
  Subtrator_Mestre Subtrator (
    .in_1(in_1), .A(in_2), .in_3(in_3), .in_4(in_4), .in_5(in_5), .B(in_6), .in_7(in_7), .in_8(in_8),
    .out_9(Subtrator_out_9), .out_10(Subtrator_out_10), .out_11(Subtrator_out_11), .out_12(Subtrator_out_12));
  Multiplicador Multiplicador (
    .in_1(in_1), .A(in_2), .in_3(in_3), .in_4(in_4), .in_5(in_5), .B(in_6), .in_7(in_7), .in_8(in_8),
    .c0(Multiplicador_c0), .c1(Multiplicador_c1), .c2(Multiplicador_c2), .c3(Multiplicador_c3));
  not not_1 (not_1_out, Comparador_aeqb);
  Comparador Comparador (
    .a0(in_1), .a1(in_2), .a2(in_3), .a3(in_4), .b0(in_5), .b1(in_6), .b2(in_7), .b3(in_8),
    .AeqB(Comparador_aeqb), .AltB_A_B(Comparador_altb_a_b), .AgtB_A_B(Comparador_agtb_a_b));
  and and_1 (and_1_out, not_1_out, Comparador_altb_a_b);
  Multiplexador_4 multiplexador_4_1 (
    .in_1(Somador_out_9), .in_2(Subtrator_out_9), .in_3(Multiplicador_c0), .in_4(and_1_out),
    .in_5(Somador_out_10), .in_6(Subtrator_out_10), .in_7(Multiplicador_c1), .in_8(Comparador_agtb_a_b),
    .in_9(Somador_out_11), .in_10(Subtrator_out_11), .in_11(Multiplicador_c2), .in_12(1'b0),
    .in_13(Somador_out_12), .in_14(Subtrator_out_12), .in_15(Multiplicador_c3), .in_16(1'b0), .in_17(in_9),
    .in_18(_0___Soma), .out_19(out_11), .out_20(out_12), .out_21(out_13), .out_22(out_14));

  // Notes on the sheet:
  //   =
  //   a < b
  //   a > b
  //   1 = Subtraçao
  //   2 = Multiplicação
  //   3 = Comparação
  //   0: A = B
  //   1: A < B
  //   2: A > B
endmodule

module Ula_Simples (
  input  [3:0] in_1,
  input  [3:0] in_2,
  input  _0___Soma,
  input  in_4,
  output [3:0] out_5
);

  ULA Ula (
    .in_1(in_1[0]), .in_2(in_1[1]), .in_3(in_1[2]), .in_4(in_1[3]), .in_5(in_2[0]), .in_6(in_2[1]),
    .in_7(in_2[2]), .in_8(in_2[3]), .in_9(_0___Soma), ._0___Soma(in_4), .out_11(out_5[0]), .out_12(out_5[1]),
    .out_13(out_5[2]), .out_14(out_5[3]));

  // Notes on the sheet:
  //   1 = Subtraçao
  //   2 = Multiplicação
  //   3 = Comparação
  //   0: A = B
  //   1: A < B
  //   2: A > B
endmodule

module Registrador (
  input  Input,
  input  in_2,
  output Q,
  output Q_prime
);

  wire and_1_out, clock_1_out, nand_1_out, nand_2_out, not_1_out;

  Clock clock_1 (.out(clock_1_out));
  and and_1 (and_1_out, clock_1_out, in_2);
  nand nand_1 (nand_1_out, Input, and_1_out);
  nand nand_2 (nand_2_out, and_1_out, not_1_out);
  not not_1 (not_1_out, Input);
  nor nor_1 (Q, nand_1_out, Q_prime);
  nor nor_2 (Q_prime, Q, nand_2_out);

  // Notes on the sheet:
  //   Clock
  //   Controlador
  //   S
  //   R
endmodule

module Registrador_de_4 (
  input  in_1,
  input  in_2,
  input  in_3,
  input  in_4,
  input  in_5,
  output out_6,
  output out_7,
  output out_8,
  output out_9
);

  Registrador registrador_1 (.Input(in_1), .in_2(in_5), .Q(out_6));  // open: Q_prime
  Registrador registrador_2 (.Input(in_2), .in_2(in_5), .Q(out_7));  // open: Q_prime
  Registrador registrador_3 (.Input(in_3), .in_2(in_5), .Q(out_8));  // open: Q_prime
  Registrador registrador_4 (.Input(in_4), .in_2(in_5), .Q(out_9));  // open: Q_prime
endmodule

module ula_e_registrador (
  input  Enable_1,
  input  in_2,
  input  in_3,
  input  in_4,
  input  in_5,
  input  in_6,
  input  in_7,
  input  in_8,
  input  in_9,
  input  in_10,
  input  in_11,
  input  _0___Soma
);

  wire [3:0] registrador_de_4_1_out_6, registrador_de_4_2_out_6, registrador_de_4_3_out_6,
       ula_simples_1_out_5;

  Registrador_de_4 registrador_de_4_1 (
    .in_1(in_2), .in_2(in_3), .in_3(in_4), .in_4(in_5), .in_5(Enable_1), .out_6(registrador_de_4_1_out_6[0]),
    .out_7(registrador_de_4_1_out_6[1]), .out_8(registrador_de_4_1_out_6[2]),
    .out_9(registrador_de_4_1_out_6[3]));
  Registrador_de_4 registrador_de_4_2 (
    .in_1(in_6), .in_2(in_7), .in_3(in_8), .in_4(in_9), .in_5(_0___Soma),
    .out_6(registrador_de_4_2_out_6[0]), .out_7(registrador_de_4_2_out_6[1]),
    .out_8(registrador_de_4_2_out_6[2]), .out_9(registrador_de_4_2_out_6[3]));
  Registrador_de_4 registrador_de_4_3 (
    .in_1(ula_simples_1_out_5[0]), .in_2(ula_simples_1_out_5[1]), .in_3(ula_simples_1_out_5[2]),
    .in_4(ula_simples_1_out_5[3]), .in_5(_0___Soma), .out_6(registrador_de_4_3_out_6[0]),
    .out_7(registrador_de_4_3_out_6[1]), .out_8(registrador_de_4_3_out_6[2]),
    .out_9(registrador_de_4_3_out_6[3]));
  Ula_Simples ula_simples_1 (
    .in_1(registrador_de_4_1_out_6), .in_2(registrador_de_4_2_out_6), ._0___Soma(_0___Soma),
    .in_4(_0___Soma), .out_5(ula_simples_1_out_5));
  Hex_Digit_Display hex_digit_display_1 (.value(registrador_de_4_3_out_6));  // open: dp

  assign in_10 = _0___Soma;
  assign in_11 = _0___Soma;

  // Notes on the sheet:
  //   Enable 2
  //   1 = Subtraçao
  //   2 = Multiplicação
  //   3 = Comparação
  //   0: A = B
  //   1: A < B
  //   2: A > B
endmodule

module CPU (
  input  Enable,
  input  Enable_2,
  input  Reset,
  input  in_4,
  input  _0___Soma,
  input  Leitura_Escrita
);

  wire clock_1_out;
  wire [3:0] counter_1_q, ram_1_data, register_1_q, register_2_q, ula_simples_1_out_5;

  Counter #(.width(4), .max('hf)) counter_1 (
    .Q(counter_1_q), .clk(clock_1_out), .clr(Reset));  // open: load, D, count, carry
  Clock clock_1 (.out(clock_1_out));
  RAM #(.addrWidth(4), .dataWidth(4), .bus("separate")) ram_1 (
    .addr(counter_1_q), .din(ula_simples_1_out_5), .data(ram_1_data), .str(Leitura_Escrita), .clk(clock_1_out));  // open: sel, ld, clr
  Register #(.width(4)) register_1 (.D(ram_1_data), .en(Enable_2), .Q(register_1_q), .clk(clock_1_out));  // open: clr
  Register #(.width(4)) register_2 (.D(ram_1_data), .en(Enable), .Q(register_2_q), .clk(clock_1_out));  // open: clr
  Ula_Simples ula_simples_1 (
    .in_1(register_1_q), .in_2(register_2_q), ._0___Soma(in_4), .in_4(_0___Soma), .out_5(ula_simples_1_out_5));

  // Notes on the sheet:
  //   Clock
  //   1 = Subtraçao
  //   2 = Multiplicação
  //   3 = Comparação
  //   0: A = B
  //   1: A < B
  //   2: A > B
endmodule

module cres_assincrono (
);

  wire and_1_out, clock_1_out;
  wire [0:0] j_k_ff_3_q;
  wire [3:0] j_k_ff_1_q;

  Clock clock_1 (.out(clock_1_out));
  J_K_Flip_Flop #(.trigger("falling")) j_k_ff_1 (
    .J(1'b1), .clk(clock_1_out), .K(1'b1), .Q(j_k_ff_1_q[0]), .reset(and_1_out));  // open: Qn, preset, en
  J_K_Flip_Flop #(.trigger("falling")) j_k_ff_2 (
    .J(1'b1), .clk(j_k_ff_1_q[0]), .K(1'b1), .Q(j_k_ff_1_q[1]), .reset(and_1_out));  // open: Qn, preset, en
  J_K_Flip_Flop #(.trigger("falling")) j_k_ff_3 (
    .J(1'b1), .clk(and_1_out), .K(1'b1), .Q(j_k_ff_3_q[0]));  // open: Qn, preset, en, reset
  J_K_Flip_Flop #(.trigger("falling")) j_k_ff_4 (
    .J(1'b1), .clk(j_k_ff_1_q[1]), .K(1'b1), .Q(j_k_ff_1_q[2]), .reset(and_1_out));  // open: Qn, preset, en
  J_K_Flip_Flop #(.trigger("falling")) j_k_ff_5 (
    .J(1'b1), .clk(j_k_ff_1_q[2]), .K(1'b1), .Q(j_k_ff_1_q[3]), .reset(and_1_out));  // open: Qn, preset, en
  and and_1 (and_1_out, j_k_ff_1_q[3], ~j_k_ff_1_q[0], j_k_ff_1_q[1], ~j_k_ff_1_q[2]);  // AND_Gate
  Hex_Digit_Display hex_digit_display_1 (.value({3'b000, j_k_ff_3_q[0]}));  // open: dp
  Hex_Digit_Display hex_digit_display_2 (.value(j_k_ff_1_q));  // open: dp
endmodule
