// Logisim project somador_assincrono_0_99.circ as structural Verilog: 1 circuit, main circuit main
module main (
);

  wire and_1_out, and_2_out, clock_1_out;
  wire [3:0] j_k_ff_1_q, j_k_ff_2_q;

  Clock clock_1 (.out(clock_1_out));
  J_K_Flip_Flop #(.trigger("falling")) j_k_ff_1 (
    .J(1'b1), .clk(clock_1_out), .K(1'b1), .Q(j_k_ff_1_q[0]), .reset(and_1_out));  // open: Qn, preset, en
  J_K_Flip_Flop #(.trigger("falling")) j_k_ff_2 (
    .J(1'b1), .clk(j_k_ff_1_q[3]), .K(1'b1), .Q(j_k_ff_2_q[0]), .reset(and_2_out));  // open: Qn, preset, en
  J_K_Flip_Flop #(.trigger("falling")) j_k_ff_3 (
    .J(1'b1), .clk(j_k_ff_1_q[0]), .K(1'b1), .Q(j_k_ff_1_q[1]), .reset(and_1_out));  // open: Qn, preset, en
  J_K_Flip_Flop #(.trigger("falling")) j_k_ff_4 (
    .J(1'b1), .clk(j_k_ff_2_q[0]), .K(1'b1), .Q(j_k_ff_2_q[1]), .reset(and_2_out));  // open: Qn, preset, en
  J_K_Flip_Flop #(.trigger("falling")) j_k_ff_5 (
    .J(1'b1), .clk(j_k_ff_1_q[1]), .K(1'b1), .Q(j_k_ff_1_q[2]), .reset(and_1_out));  // open: Qn, preset, en
  J_K_Flip_Flop #(.trigger("falling")) j_k_ff_6 (
    .J(1'b1), .clk(j_k_ff_2_q[1]), .K(1'b1), .Q(j_k_ff_2_q[2]), .reset(and_2_out));  // open: Qn, preset, en
  and and_1 (and_1_out, ~j_k_ff_1_q[0], j_k_ff_1_q[1], ~j_k_ff_1_q[2], j_k_ff_1_q[3]);  // AND_Gate
  and and_2 (and_2_out, ~j_k_ff_2_q[0], j_k_ff_2_q[1], ~j_k_ff_2_q[2], j_k_ff_2_q[3]);  // AND_Gate
  J_K_Flip_Flop #(.trigger("falling")) j_k_ff_7 (
    .J(1'b1), .clk(j_k_ff_1_q[2]), .K(1'b1), .Q(j_k_ff_1_q[3]), .reset(and_1_out));  // open: Qn, preset, en
  J_K_Flip_Flop #(.trigger("falling")) j_k_ff_8 (
    .J(1'b1), .clk(j_k_ff_2_q[2]), .K(1'b1), .Q(j_k_ff_2_q[3]), .reset(and_2_out));  // open: Qn, preset, en
  Hex_Digit_Display hex_digit_display_1 (.value(j_k_ff_2_q));  // open: dp
  Hex_Digit_Display hex_digit_display_2 (.value(j_k_ff_1_q));  // open: dp
endmodule
